# Fritzing sketch PYL Wiring (saved by Fritzing 0.8.7b)
breadboards: 1

parts:
  J1 = Raspberry Pi Header 40pin [package=THT]  # not connected
  S2 = Round Pushbutton
  S3 = Round Pushbutton
  S7 = Square Pushbutton
  S8 = Square Pushbutton
  S9 = Square Pushbutton
  LED1 = LED - 5mm [color="Red (633nm)" package="5 mm [THT]"]
  LED2 = LED - 5mm [color="Red (633nm)" package="5 mm [THT]"]

nets:
  N1: S2.leg0, S3.leg0, S7.leg0, S8.leg0, S9.leg0, LED1.anode, LED2.anode

custom parts:
  Raspberry Pi Header 40pin: Raspberry Pi 40 pin header - for creating your own shields. (Mar 2020, bb: make breadboard friendly (.4in pin spacing) and add labels. Schematic add labels. PCB make oblong pins to allow routing traces between the pins.)
